# Fritzing sketch Layout_Breadboard (saved by Fritzing 0.9.10b)
circuit board: 8.46667cm x 5.64444cm
breadboards: 1

parts:
  Arduino_RP2040_Connect = Arduino Nano (Rev3.0)
  SD-Card_Holder = Adafruit SDIO microSD Breakout
  GPS_Modul = Adafruit Ultimate GPS v3 [part_number="Adafruit #746"]

nets:
  GND: Arduino_RP2040_Connect.GND, SD-Card_Holder.GND, GPS_Modul.GND
  N1: Arduino_RP2040_Connect.D10, SD-Card_Holder.CS
  N2: Arduino_RP2040_Connect.D11/MOSI, SD-Card_Holder.DI
  N3: Arduino_RP2040_Connect.D12/MISO, SD-Card_Holder.DO
  3V3: Arduino_RP2040_Connect.3V3, SD-Card_Holder.3.3V, GPS_Modul.VIN
  N4: Arduino_RP2040_Connect.D13/SCK, SD-Card_Holder.SCLK

notes:
  MotoData V 0-1

custom parts:
  Adafruit Ultimate GPS v3: We carry a few different GPS modules here in the Adafruit shop, but none that satisfied our every desire - that's why we designed this little GPS breakout board. We believe this is the Ultimate GPS module, so we named it that. It's got everything you want and more: -165 dBm sensitivity, 10 Hz updates, 66 channels 5V friendly design and only 20mA current draw Breadboard friendly + two mounting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
